# Fritzing sketch ArduinoNano-DualRelay5V (saved by Fritzing 0.9.3b)
breadboards: 1

parts:
  5_Volt_USB = Power plug
  U2 = 2-Channel 5v Relay Shield [package=relay-2ch5v10a]
  Garage_Light = Momentary Switch [package=ksa_sealed_tac_switch]
  Garage_Switch = Momentary Switch [package=ksa_sealed_tac_switch]
  Arduino_Nano_v3 = Arduino Nano (Rev3.0) [part_number="with ENC28J60 Ethernet Sheild"]

nets:
  GND: 5_Volt_USB.GND, U2.GND, Arduino_Nano_v3.GND
  VCC: 5_Volt_USB.VCC, U2.VCC, Arduino_Nano_v3.VIN
  N1: U2.IN1, Arduino_Nano_v3.D2
  N2: U2.IN2, Arduino_Nano_v3.D3
  N3: U2.K1-In, Garage_Switch.1
  N4: U2.K1-Off, Garage_Switch.2
  N5: U2.K1-On, U2.K2-On
  N6: U2.K2-In, Garage_Light.1
  N7: U2.K2-Off, Garage_Light.2

custom parts:
  2-Channel 5v Relay Shield: 2 Channel 5v Relay Shield w. 2x SPD-06VDC-SD-C
