# Fritzing sketch ArduinoNano-ENC28J60-DualRelay5V (saved by Fritzing 0.9.3b)
breadboards: 1

parts:
  5_Volt_USB = Power plug
  U2 = 2-Channel 5v Relay Shield [package=relay-2ch5v10a]
  Garage_Light = Momentary Switch [package=ksa_sealed_tac_switch]
  Garage_Switch = Momentary Switch [package=ksa_sealed_tac_switch]
  Arduino_Nano_v3 = Arduino Nano (Rev3.0)
  ENC28J60_Mini1 = ENC28J60 Mini

nets:
  GND: 5_Volt_USB.GND, U2.GND, Arduino_Nano_v3.GND, ENC28J60_Mini1.GND
  VCC: 5_Volt_USB.VCC, U2.VCC, Arduino_Nano_v3.VIN, ENC28J60_Mini1.VCC
  N1: U2.IN1, Arduino_Nano_v3.D2
  N2: U2.IN2, Arduino_Nano_v3.D3
  N3: U2.K1-In, Garage_Switch.1
  N4: U2.K1-Off, Garage_Switch.2
  N5: U2.K1-On, U2.K2-On
  N6: U2.K2-In, Garage_Light.1
  N7: U2.K2-Off, Garage_Light.2
  N8: Arduino_Nano_v3.D10, ENC28J60_Mini1.CS
  N9: Arduino_Nano_v3.D11/MOSI, ENC28J60_Mini1.SI
  N10: Arduino_Nano_v3.D12/MISO, ENC28J60_Mini1.SO
  N11: Arduino_Nano_v3.D13/SCK, ENC28J60_Mini1.SCK

custom parts:
  2-Channel 5v Relay Shield: 2 Channel 5v Relay Shield w. 2x SPD-06VDC-SD-C
