# Fritzing sketch ArduinoUNO-ENC28J60-DualRelay5V (saved by Fritzing 0.9.3b)

parts:
  U2 = 2-Channel 5v Relay Shield [package=relay-2ch5v10a]
  Garage_Light = Momentary Switch [package=ksa_sealed_tac_switch]
  Garage_Switch = Momentary Switch [package=ksa_sealed_tac_switch]
  Part1 = Arduino Uno (Rev3)
  ENC28J60_Mini1 = ENC28J60 Mini

nets:
  VCC: U2.VCC, Part1.5V, ENC28J60_Mini1.VCC
  GND: U2.GND, Part1.GND, ENC28J60_Mini1.GND
  N1: U2.IN1, Part1.D2
  N2: U2.IN2, Part1.D3_PWM
  N3: U2.K1-In, Garage_Switch.1
  N4: U2.K1-Off, Garage_Switch.2
  N5: U2.K1-On, U2.K2-On
  N6: U2.K2-In, Garage_Light.1
  N7: U2.K2-Off, Garage_Light.2
  N8: Part1.D10_PWM/SS, ENC28J60_Mini1.CS
  N9: Part1.D11_PWM/MOSI, ENC28J60_Mini1.SI
  N10: Part1.D12/MISO, ENC28J60_Mini1.SO
  N11: Part1.D13/SCK, ENC28J60_Mini1.SCK

custom parts:
  2-Channel 5v Relay Shield: 2 Channel 5v Relay Shield w. 2x SPD-06VDC-SD-C
