# Fritzing sketch IRSender (saved by Fritzing 0.9.3b)
breadboards: 1

parts:
  5_Volt_USB = Power plug  # not connected
  Part1 = SparkFun ESP8266 Thing
  TSAL6400 = smd LED [color="Infrared (940nm)" package="0805 [SMD]"]
  LED4 = smd LED [color="Infrared (940nm)" package="0805 [SMD]"]

nets:
  N1: Part1.GND, TSAL6400.cathode
  N2: Part1.GPIO4, LED4.anode
  N3: TSAL6400.anode, LED4.cathode
